# Fritzing sketch schematics (saved by Fritzing 0.9.3b)

parts:
  Part1 = Arduino Uno (Rev3) - ICSP
  A1 = tds-sensor-meter-v1.0_1
  U1 = Turbidity Sensor Probe [package=THT]
  M1 = PH meter with sensor in breadboard [package=THT]
  Part3 = SRF05 Ultrasonic Rangefinder
  Part4 = SRF05 Ultrasonic Rangefinder
  A2 = 6 channel relay module
  U2 = ESP32S-HiLetgo [part_number=ESP32S-HiLetgo]
  Keypad4x3 = Keypad Membran 4x4
  A3 = Electropeak 2.4in LCD

nets:
  N1: Part1.A0, M1.pin3
  N2: Part1.A1, A1.pin1
  N3: Part1.A2, U1.VCC
  N4: Part1.D9_PWM, A2.Pin_4
  N5: Part1.D10_PWM/SS, A2.Pin_5
  N6: Part1.D11_PWM/MOSI, A2.Pin_6
  N7: Part1.D12/MISO, A2.Pin_7
  GND: Part1.GND, A1.pin3, U1.pin2, M1.pin1, Part3.GND, Part4.GND, A2.Pin_1, A2.Pin_9, U2.GND, A3.Pin_2
  N8: Part1.D0/RX, U2.GPIO36
  N9: Part1.D1/TX, U2.EN
  N10: Part1.D2, Part3.Echo
  N11: Part1.D3_PWM, Part3.Trig
  N12: Part1.D4, Part4.Echo
  N13: Part1.D5_PWM, Part4.Trig
  N14: Part1.D6_PWM, A2.Pin_2
  N15: Part1.D7, A2.Pin_3
  VCC: Part1.5V, A1.pin2, U1.pin1, M1.pin2, Part3.VCC, Part4.VCC, A2.Pin_8, A2.Pin_10, U2.VIN
  N16: U2.3.3, A3.Pin_8
  N17: U2.GPIO34, Keypad4x3.Pin8
  N18: U2.GPIO35, Keypad4x3.Pin7
  N19: U2.GPIO32, Keypad4x3.Pin6
  N20: U2.GPIO33, Keypad4x3.Pin5
  N21: U2.GPIO25, Keypad4x3.Pin4
  N22: U2.GPIO26, Keypad4x3.Pin3
  N23: U2.GPIO27, Keypad4x3.Pin2
  N24: U2.GPIO14, Keypad4x3.Pin1
  N25: U2.GPIO5, A3.Pin_3
  N26: U2.GPIO18, A3.Pin_7
  N27: U2.GPIO21, A3.Pin_5
  N28: U2.GPIO22, A3.Pin_4
  N29: U2.GPIO23, A3.Pin_6

custom parts:
  : TDS Meter V1.0 Development Board Water Meter Filter Measuring Water Sensor Module.
  Turbidity Sensor Probe: Turbidity sensor probe to the DFRobot measure module.
  PH meter with sensor in breadboard: analog ph sensor module.
  6 channel relay module: 6 Channel 5V Relay Board Module Optocoupler LED.
  ESP32S-HiLetgo: HiLetgo ESP-WROOM-32 ESP32 ESP-32S Development Board 2.4GHz Dual-Mode WiFi + Bluetooth Dual Cores Microcontroller The ESP32 integrated with Antenna switches, RF Balun, power amplifiers, low-noise amplifiers, filters, and management modules, and the entire solution occupies the least area of PCB. 2.4 GHz Wi-Fi plus Bluetooth dual-mode chip, with TSMC Ultra-low power consumption 40nm technology,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
  Keypad Membran 4x4: Membrane Keypad 4x4 Matrix
  Electropeak 2.4in LCD: 2.4 inch Touch TFT LCD Display Shield for Arduino UNO/Mega.
